# Fritzing sketch Prueba acelerometro (saved by Fritzing 0.9.3b)

parts:
  Part1 = Triple Axis Accelerometer Breakout - ADXL335
  Part2 = Arduino Mega 2560 (Rev3)

nets:
  N1: Part1.ZOUT, Part2.A2
  N2: Part1.YOUT, Part2.A1
  N3: Part1.XOUT, Part2.A0
  GND: Part1.GND, Part2.GND
  VCC: Part1.VCC, Part2.3V3
