# Fritzing sketch Prueba de motores (saved by Fritzing 0.9.3b)
breadboards: 1

parts:
  Componente1 = Arduino Mega 2560 (Rev3)
  M2 = DC Motor
  S1 = Pushbutton [package="[THT]"]
  S2 = Pushbutton [package="[THT]"]
  S3 = Pushbutton [package="[THT]"]
  S4 = Pushbutton [package="[THT]"]
  IC4 = L293D [package=THT]
  R1 = Resistor [tolerance=±5% resistance=220 package=THT]
  R2 = Resistor [tolerance=±5% resistance=220 package=THT]
  R3 = Resistor [tolerance=±5% resistance=220 package=THT]
  R4 = Resistor [tolerance=±5% resistance=220 package=THT]
  M1 = DC Motor
  VCC1 = Battery block 9V

nets:
  N1: Componente1.D11_PWM, IC4.In_1
  N2: Componente1.D10_PWM, IC4.In_2
  N3: Componente1.D9_PWM, IC4.In_4
  N4: Componente1.D8_PWM, IC4.In_3
  N5: Componente1.5V, S1.Pin_1, S1.Pin_2, S2.Pin_1, S2.Pin_2, S3.Pin_1, S3.Pin_2, S4.Pin_1, S4.Pin_2, IC4.Enable_1, IC4.Enable_2, IC4.+V
  N6: Componente1.GND, IC4.0V, R1.Pin_0, R2.Pin_0, R3.Pin_0, R4.Pin_0, VCC1.-
  N7: Componente1.D2_PWM, S1.Pin_3, S1.Pin_4, R1.Pin_1
  N8: Componente1.D3_PWM, S2.Pin_3, S2.Pin_4, R2.Pin_1
  N9: Componente1.D4_PWM, S4.Pin_3, S4.Pin_4, R3.Pin_1
  N10: Componente1.D5_PWM, S3.Pin_3, S3.Pin_4, R4.Pin_1
  N11: M2.pin_1, IC4.Out_4_(_Controlled_by_Enable_2_)
  N12: M2.pin_2, IC4.Out_3_(_Controlled_by_Enable_2_)
  N13: IC4.Out_1_(_Controlled_by_Enable_1_), M1.pin_1
  N14: IC4.Out_2_(_Controlled_by_Enable_1_), M1.pin_2
  N15: IC4.+Vmotor, VCC1.+

notes:
  izquierda y derecha
  Atras y adelante
  Motor derecha
  Motor izquierda

// code stored in the sketch: motores (giro a la derecha e izquierda).fzz.ino
const int buttonf = 3;
const int buttonb = 2;
const int buttonleft = 4;
const int buttonright = 5;
int buttonstatef = 0;
int buttonstateb = 0;
int buttonstateleft = 0;
int buttonstateright = 0;

const int rightf = 11;
const int rightb = 10;
const int leftf = 9;
const int leftb = 8;

void setup() {

  pinMode(buttonf, INPUT);
  pinMode(buttonb, INPUT);
	pinMode(buttonleft, INPUT);
	pinMode(buttonright, INPUT);
  pinMode(rightf, OUTPUT);
  pinMode(rightb, OUTPUT);
  pinMode(leftf, OUTPUT);
  pinMode(leftb, OUTPUT);

}

void loop() {

  buttonstatef = digitalRead(buttonf);
  buttonstateb = digitalRead(buttonb);
	buttonstateleft = digitalRead(buttonleft);
	buttonstateright = digitalRead(buttonright);


  if (buttonstatef == HIGH && buttonstateb == LOW && buttonstateleft == LOW && buttonstateright == LOW){
    digitalWrite(rightf, HIGH);
    digitalWrite(rightb, LOW);
    digitalWrite(leftf, HIGH);
    digitalWrite(leftb, LOW);   
  } else if (buttonstatef == LOW && buttonstateb == HIGH && buttonstateleft == LOW && buttonstateright == LOW ){
    digitalWrite(rightf, LOW);
    digitalWrite(rightb, HIGH);
    digitalWrite(leftf, LOW);
    digitalWrite(leftb, HIGH); 
	} else if (buttonstatef == LOW && buttonstateb == LOW && buttonstateleft == HIGH && buttonstateright == LOW){
		digitalWrite(rightf, HIGH);
    digitalWrite(rightb, LOW);
    digitalWrite(leftf, LOW);
    digitalWrite(leftb, HIGH);
	}	else if (buttonstatef == LOW && buttonstateb == LOW && buttonstateleft == LOW && buttonstateright == HIGH){
		digitalWrite(rightf, LOW);
    digitalWrite(rightb, HIGH);
    digitalWrite(leftf, HIGH);
    digitalWrite(leftb, LOW);
	} else {
    digitalWrite(rightf, LOW);
    digitalWrite(rightb, LOW);
    digitalWrite(leftf, LOW);
    digitalWrite(leftb, LOW);
  }

}
