# Fritzing sketch Prueba_de_motores_con_acelerometro (saved by Fritzing 0.9.3b)
breadboards: 1

parts:
  Componente1 = Arduino Mega 2560 (Rev3)
  M2 = DC Motor
  IC4 = L293D [package=THT]
  M1 = DC Motor
  VCC1 = Battery block 9V
  Part1 = Triple Axis Accelerometer Breakout - ADXL335

nets:
  N1: Componente1.A2, Part1.ZOUT
  N2: Componente1.D11_PWM, IC4.In_1
  N3: Componente1.D10_PWM, IC4.In_2
  N4: Componente1.D9_PWM, IC4.In_4
  N5: Componente1.D8_PWM, IC4.In_3
  3V3: Componente1.3V3, Part1.VCC
  N6: Componente1.5V, IC4.Enable_1, IC4.Enable_2, IC4.+V
  GND: Componente1.GND, IC4.0V, VCC1.-, Part1.GND
  N7: M2.pin_1, IC4.Out_4_(_Controlled_by_Enable_2_)
  N8: M2.pin_2, IC4.Out_3_(_Controlled_by_Enable_2_)
  N9: IC4.Out_1_(_Controlled_by_Enable_1_), M1.pin_1
  N10: IC4.Out_2_(_Controlled_by_Enable_1_), M1.pin_2
  N11: IC4.+Vmotor, VCC1.+

notes:
  Motor derecha
  Motor izquierda

// code stored in the sketch: motores (giro a la derecha e izquierda).fzz.ino
const int buttonf = 3;
const int buttonb = 2;
const int buttonleft = 4;
const int buttonright = 5;
int buttonstatef = 0;
int buttonstateb = 0;
int buttonstateleft = 0;
int buttonstateright = 0;

const int rightf = 11;
const int rightb = 10;
const int leftf = 9;
const int leftb = 8;

void setup() {

  pinMode(buttonf, INPUT);
  pinMode(buttonb, INPUT);
	pinMode(buttonleft, INPUT);
	pinMode(buttonright, INPUT);
  pinMode(rightf, OUTPUT);
  pinMode(rightb, OUTPUT);
  pinMode(leftf, OUTPUT);
  pinMode(leftb, OUTPUT);

}

void loop() {

  buttonstatef = digitalRead(buttonf);
  buttonstateb = digitalRead(buttonb);
	buttonstateleft = digitalRead(buttonleft);
	buttonstateright = digitalRead(buttonright);


  if (buttonstatef == HIGH && buttonstateb == LOW && buttonstateleft == LOW && buttonstateright == LOW){
    digitalWrite(rightf, HIGH);
    digitalWrite(rightb, LOW);
    digitalWrite(leftf, HIGH);
    digitalWrite(leftb, LOW);   
  } else if (buttonstatef == LOW && buttonstateb == HIGH && buttonstateleft == LOW && buttonstateright == LOW ){
    digitalWrite(rightf, LOW);
    digitalWrite(rightb, HIGH);
    digitalWrite(leftf, LOW);
    digitalWrite(leftb, HIGH); 
	} else if (buttonstatef == LOW && buttonstateb == LOW && buttonstateleft == HIGH && buttonstateright == LOW){
		digitalWrite(rightf, HIGH);
    digitalWrite(rightb, LOW);
    digitalWrite(leftf, LOW);
    digitalWrite(leftb, HIGH);
	}	else if (buttonstatef == LOW && buttonstateb == LOW && buttonstateleft == LOW && buttonstateright == HIGH){
		digitalWrite(rightf, LOW);
    digitalWrite(rightb, HIGH);
    digitalWrite(leftf, HIGH);
    digitalWrite(leftb, LOW);
	} else {
    digitalWrite(rightf, LOW);
    digitalWrite(rightb, LOW);
    digitalWrite(leftf, LOW);
    digitalWrite(leftb, LOW);
  }

}
