# Fritzing sketch Prueba de sensor de colores (saved by Fritzing 0.9.3b)

parts:
  e-radionica1 = TCS230 Color Sensor [part_number=101209]
  Componente1 = Arduino Mega 2560 (Rev3)

nets:
  GND: e-radionica1.Gnd, Componente1.GND
  N1: e-radionica1.S1, Componente1.D5_PWM
  N2: e-radionica1.S0, Componente1.D4_PWM
  N3: e-radionica1.S3, Componente1.D6_PWM
  N4: e-radionica1.S2, Componente1.D7_PWM
  N5: e-radionica1.Out, Componente1.D8_PWM
  VCC: e-radionica1.Vcc, Componente1.5V

custom parts:
  TCS230 Color Sensor: TCS230
